# Fritzing sketch attack4-wiring (saved by Fritzing 1.0.6)

parts:
  RP2040-Zero = Waveshare rp2040-zero tht [package=THT]
  Safe_contacts = Safe GPIO contacts
  R_A = Resistor [resistance=220 package=THT]
  R_B = Resistor [resistance=220 package=THT]

nets:
  N1: RP2040-Zero.Pin_2, Safe_contacts.GND
  N2: RP2040-Zero.Pin_18, Safe_contacts.SENSE_GPIO10
  N3: RP2040-Zero.Pin_19, R_A.Pin_0
  N4: RP2040-Zero.Pin_20, Safe_contacts.SW_GPIO28
  N5: RP2040-Zero.Pin_21, R_B.Pin_0
  N6: Safe_contacts.B_GPIO27, R_B.Pin_1
  N7: Safe_contacts.A_GPIO29, R_A.Pin_1

custom parts:
  Waveshare rp2040-zero tht: .RP2040-Zero, A Low-Cost, High-Performance Pico-Like MCU Board Based On Raspberry Pi Microcontroller RP2040. This varant is THT without the extra connections.
  Safe GPIO contacts: Known connection points, not a reconstructed safe PCB
